// Logisim project abcco8r2.circ as structural Verilog: 16 circuits, main circuit main
module main (
);

  wire button_1_out, button_2_out, button_3_out, button_4_out, button_5_out, button_6_out, button_7_out,
       button_8_out, clock_1_out, cpu_1_carry, cpu_1_clock_out, cpu_1_microcode_jump,
       cpu_1_program_counter_increment, cpu_1_waiting, entry_1__0_2, entry_1__1_2, entry_1__2_2,
       entry_1__3_2, entry_1__4_2, entry_1__5_2, entry_1__6_2, entry_1__7_2, INT_out, RST_out;
  wire [7:0] cpu_1_address_2, entry_1_value;
  wire [15:0] rom_1_data;

  Clock clock_1 (.out(clock_1_out));
  Button RST (.out(RST_out));
  Button INT (.out(INT_out));
  Button button_1 (.out(button_1_out));
  Button button_2 (.out(button_2_out));
  Button button_3 (.out(button_3_out));
  Button button_4 (.out(button_4_out));
  LED led_1 (.in(entry_1__0_2));
  LED led_2 (.in(entry_1__2_2));
  LED led_3 (.in(entry_1__3_2));
  LED led_4 (.in(entry_1__1_2));
  Button button_5 (.out(button_5_out));
  Button button_6 (.out(button_6_out));
  Button button_7 (.out(button_7_out));
  Button button_8 (.out(button_8_out));
  Entry entry_1 (
    .Value(entry_1_value), ._0(button_4_out), ._1(button_1_out), ._2(button_2_out), ._3(button_3_out),
    ._4(button_8_out), ._5(button_7_out), ._6(button_6_out), ._7(button_5_out), ._0_2(entry_1__0_2),
    ._1_2(entry_1__1_2), ._2_2(entry_1__2_2), ._3_2(entry_1__3_2), ._4_2(entry_1__4_2), ._5_2(entry_1__5_2),
    ._6_2(entry_1__6_2), ._7_2(entry_1__7_2));  // open: Zero_all, Enable, One_all
  LED led_5 (.in(entry_1__6_2));
  LED led_6 (.in(entry_1__4_2));
  LED led_7 (.in(entry_1__7_2));
  LED led_8 (.in(entry_1__5_2));
  ROM #(.dataWidth(16)) rom_1 (.addr(cpu_1_address_2), .data(rom_1_data));  // open: sel
  CPU cpu_1 (
    .Clock_in(clock_1_out), .Microcode(rom_1_data), .Reset(RST_out), .Interrupt(INT_out),
    .Interrupt_flag(entry_1_value), .Address_2(cpu_1_address_2), .Microcode_jump(cpu_1_microcode_jump),
    .Carry(cpu_1_carry), .Clock_out(cpu_1_clock_out),
    .Program_counter_increment(cpu_1_program_counter_increment), .Waiting(cpu_1_waiting));  // open: Data_bus, Address, Bus, Register_select
  LED Microcode_jump (.in(cpu_1_microcode_jump));
  LED Carry (.in(cpu_1_carry));
  LED Clock_out (.in(cpu_1_clock_out));
  LED PCI (.in(cpu_1_program_counter_increment));
  LED Waiting (.in(cpu_1_waiting));

  // Notes on the sheet:
  //   contents of rom_1 (hex, n*v repeats v):
  //   0 30d 212 301 210 300 211 113 2ff 211 800 512 113 2ff 210 800 512 607 900 a00
endmodule

// ABCco8\nVer. 2
module CPU (
  input  [7:0] Data_bus,
  input  Reset,
  input  Interrupt,
  input  Clock_in,
  input  [7:0] Address,
  input  [15:0] Microcode,
  input  [7:0] Interrupt_flag,
  output [7:0] Bus,
  output [7:0] Address_2,
  output [7:0] Register_select,
  output Waiting,
  output Microcode_jump,
  output Carry,
  output Clock_out,
  output Program_counter_increment
);

  wire alu_v2_1_reading, button_1_out, button_2_out, button_3_out, button_4_out, button_5_out, button_6_out,
       button_7_out, button_8_out, button_9_out, button_10_out, entry_1__0_2, entry_1__1_2, entry_1__2_2,
       entry_1__3_2, entry_1__4_2, entry_1__5_2, entry_1__6_2, entry_1__7_2, Manual_interrupt_out,
       mcu_1_register_read, mcu_1_register_write, not_1_out, or_1_out, or_2_out, rrd_1_is_reading,
       square_led_4_p1, square_led_5_p1, square_led_5_p2;
  wire [7:0] binary_to_bcd_2_p1, entry_1_value, mcu_1_bus_out, mcu_1_microcode_jump_address,
       microcode_counter_1_instruction, microcode_counter_1_parameter, register_1_q;

  Button button_1 (.out(button_1_out));
  Button button_2 (.out(button_2_out));
  Button button_3 (.out(button_3_out));
  Button button_4 (.out(button_4_out));
  Button button_5 (.out(button_5_out));
  LED led_1 (.in(entry_1__2_2));
  LED led_2 (.in(entry_1__1_2));
  LED led_3 (.in(entry_1__0_2));
  or or_1 (or_1_out, Interrupt, Manual_interrupt_out);
  Button Manual_interrupt (.out(Manual_interrupt_out));
  Button button_6 (.out(button_6_out));
  Button button_7 (.out(button_7_out));
  Button button_8 (.out(button_8_out));
  Button button_9 (.out(button_9_out));
  LED led_4 (.in(entry_1__5_2));
  LED led_5 (.in(entry_1__6_2));
  LED led_6 (.in(entry_1__4_2));
  LED led_7 (.in(entry_1__3_2));
  Register register_1 (.D(Interrupt_flag), .Q(register_1_q), .clk(or_1_out), .clr(or_2_out));  // open: en
  Button button_10 (.out(button_10_out));
  Entry entry_1 (
    .Zero_all(button_1_out), .Enable(1'b1), .One_all(button_2_out), .Value(entry_1_value), ._0(button_3_out),
    ._1(button_5_out), ._2(button_4_out), ._3(button_8_out), ._4(button_7_out), ._5(button_9_out),
    ._6(button_6_out), ._7(button_10_out), ._0_2(entry_1__0_2), ._1_2(entry_1__1_2), ._2_2(entry_1__2_2),
    ._3_2(entry_1__3_2), ._4_2(entry_1__4_2), ._5_2(entry_1__5_2), ._6_2(entry_1__6_2), ._7_2(entry_1__7_2));
  LED led_8 (.in(entry_1__7_2));
  or or_2 (or_2_out, Reset, Program_counter_increment);
  Microcode_counter microcode_counter_1 (
    .Data(Microcode), .Address(mcu_1_microcode_jump_address), .Jump(Microcode_jump), .Clock(Clock_out),
    .Reset(Reset), .Instruction(microcode_counter_1_instruction), .Parameter(microcode_counter_1_parameter),
    .Address_2(Address_2));
  MCU mcu_1 (
    .Bus_in(Data_bus), .Parameter(microcode_counter_1_parameter), .Cin_Bin(Carry), .Interrupt(or_1_out),
    .Clock(Clock_in), .Clear(or_2_out), .Microcode(microcode_counter_1_instruction), .Bus_out(mcu_1_bus_out),
    .Register_select(Register_select), .Register_read(mcu_1_register_read), .Waiting(Waiting),
    .Program_counter_increment(Program_counter_increment), .Clock_out(Clock_out),
    .Microcode_jump_address(mcu_1_microcode_jump_address), .Microcode_jump(Microcode_jump),
    .Register_write(mcu_1_register_write), .Address(Address_2), .Interrpt_flag(register_1_q));
  RRD rrd_1 (
    .Register_value(register_1_q), .Register_address(8'h42), .Select(Register_select),
    .Global_read(mcu_1_register_read), .Bus_out(Data_bus), .Is_reading(rrd_1_is_reading));
  // Square_LED square_led_1: pin names not known
  ALU_V2 alu_v2_1 (
    .Data(Data_bus), .Register_select(Register_select), .Global_write(mcu_1_register_write),
    .Global_read(mcu_1_register_read), .Clear(or_2_out), .Output(Data_bus), .Reading(alu_v2_1_reading),
    .Cout_Bout(Carry));
  // Square_LED square_led_2: pin names not known; wires that end beside it: rrd_1_is_reading, alu_v2_1_reading
  // Square_LED square_led_3: pin names not known
  // Square_LED square_led_4: pin names not known; wires that end beside it: square_led_4_p1
  // Square_LED square_led_5: pin names not known; wires that end beside it: square_led_5_p1, square_led_5_p2
  REG_BANK reg_bank_1 (
    .Bus_in(Data_bus), .Register_select(Register_select), .Write(mcu_1_register_write),
    .Read(mcu_1_register_read), .Clear(or_2_out), .PCI(Program_counter_increment), .Out(Data_bus),
    .Is_reading(square_led_4_p1));
  Cache cache_1 (
    .Bus_in(Data_bus), .Register_select(Register_select), .Clear(or_2_out), .Write(mcu_1_register_write),
    .Read(mcu_1_register_read), .Clock(Clock_out), .Bus_out(Data_bus), .Reading(square_led_5_p1));
  // Binary_to_BCD binary_to_bcd_1: pin names not known; wires that end beside it: Data_bus
  Hex_Digit_Display hex_digit_display_1 ();  // open: value, dp
  Hex_Digit_Display hex_digit_display_2 ();  // open: value, dp
  // Binary_to_BCD binary_to_bcd_2: pin names not known; wires that end beside it: binary_to_bcd_2_p1
  Register_buffer DBG (
    .Data_in(Data_bus), .Register_select(Register_select), .Address({8{1'b1}}), .Write(mcu_1_register_write),
    .Clear(or_2_out), .Data_out(binary_to_bcd_2_p1));
  RRD rrd_2 (
    .Register_value(entry_1_value), .Register_address({8{1'b1}}), .Select(Register_select),
    .Global_read(mcu_1_register_read), .Bus_out(Data_bus), .Is_reading(square_led_5_p2));
  Hex_Digit_Display hex_digit_display_3 ();  // open: value, dp
  // Binary_to_BCD binary_to_bcd_3: pin names not known; wires that end beside it: or_1_out, Program_counter_increment, Clock_out, Data_bus, Register_select, or_2_out, mcu_1_register_read, mcu_1_register_write, Data_bus, entry_1_value
  not not_1 (not_1_out, mcu_1_register_read);
  Hex_Digit_Display hex_digit_display_4 ();  // open: value, dp
  Hex_Digit_Display hex_digit_display_5 ();  // open: value, dp
  Hex_Digit_Display hex_digit_display_6 ();  // open: value, dp
  Hex_Digit_Display hex_digit_display_7 ();  // open: value, dp
  Hex_Digit_Display hex_digit_display_8 ();  // open: value, dp
  Hex_Digit_Display hex_digit_display_9 ();  // open: value, dp
  LED u_Clock_in (.in(Clock_in));
  LED PCI (.in(Program_counter_increment));
  LED u_Waiting (.in(Waiting));
  LED MJ (.in(Microcode_jump));
  LED Cout (.in(Carry));
  LED u_Clock_out (.in(Clock_out));
  assign Data_bus = not_1_out ? mcu_1_bus_out : 8'bz;  // Controlled_Buffer controlled_buffer_1
  Pull_Resistor pull_resistor_1 (.node(Data_bus));
  Hex_Digit_Display hex_digit_display_10 (.value(Data_bus[7:4]));  // open: dp
  Hex_Digit_Display hex_digit_display_11 (.value(binary_to_bcd_2_p1[7:4]));  // open: dp
  Hex_Digit_Display hex_digit_display_12 (.value(entry_1_value[7:4]));  // open: dp
  Hex_Digit_Display hex_digit_display_13 (.value(Data_bus[3:0]));  // open: dp
  Hex_Digit_Display hex_digit_display_14 (.value(binary_to_bcd_2_p1[3:0]));  // open: dp
  Hex_Digit_Display hex_digit_display_15 (.value(entry_1_value[3:0]));  // open: dp

  assign Bus = Data_bus;

  // Notes on the sheet:
  //   IFR Read
  //   ALU Read
  //   Register Read
  //   Cache Read
  //   Debug Read
endmodule

module Cache (
  input  [7:0] Bus_in,
  input  [7:0] Register_select,
  input  Clear,
  input  Write,
  input  Read,
  input  Clock,
  output [7:0] Bus_out,
  output Reading
);

  wire equ_1_e_2, equ_2_e_2;
  wire [7:0] ram_1_data, register_1_q, register_2_q;

  EQU equ_1 (.A(Register_select), .B(8'h41), .E(Write), .E_2(equ_1_e_2));
  EQU equ_2 (.A(Register_select), .B(8'h40), .E(Write), .E_2(equ_2_e_2));
  EQU equ_3 (.A(Register_select), .B(8'h40), .E(Read), .E_2(Reading));
  Register register_1 (.D(Bus_in), .Q(register_1_q), .clk(equ_1_e_2), .clr(Clear));  // open: en
  Register register_2 (.D(Bus_in), .Q(register_2_q), .clk(equ_2_e_2), .clr(Clear));  // open: en
  RAM #(.bus("separate")) ram_1 (
    .addr(register_1_q), .din(register_2_q), .data(ram_1_data), .str(equ_2_e_2), .clk(Clock), .ld(Reading),
    .clr(Clear));  // open: sel
  assign Bus_out = Reading ? ram_1_data : 8'bz;  // Controlled_Buffer controlled_buffer_1
endmodule

module MCU (
  input  [7:0] Bus_in,
  input  [7:0] Parameter,
  input  Cin_Bin,
  input  [7:0] Interrpt_flag,
  input  Interrupt,
  input  Clock,
  input  Clear,
  input  [7:0] Microcode,
  input  [7:0] Address,
  output [7:0] Bus_out,
  output [7:0] Register_select,
  output Register_read,
  output Waiting,
  output Program_counter_increment,
  output Clock_out,
  output [7:0] Microcode_jump_address,
  output Microcode_jump,
  output Register_write
);

  wire and_1_out, comparator_1_eq, comparator_2_eq, controlled_buffer_1_out, controlled_buffer_4_out,
       controlled_buffer_6_out, decoder_1_out1, decoder_1_out2, decoder_1_out3, decoder_1_out4,
       decoder_1_out5, decoder_1_out6, decoder_1_out7, decoder_1_out8, decoder_1_out9, decoder_1_out11,
       decoder_1_out12, decoder_1_out13, decoder_1_out14, decoder_1_out15, decoder_1_out16, decoder_1_out17,
       INT_out, not_1_out, not_2_out, not_3_out, not_4_out, not_5_out, or_1_out, or_2_out,
       pull_resistor_3_node, RS_out, s_r_ff_1_qn;
  wire [7:0] adder_1_out, multiplexer_1_out, multiplexer_2_out, multiplexer_4_out, multiplexer_5_out,
       multiplexer_6_out, pull_resistor_4_node, register_1_q, register_2_q;
  wire [7:1] undriven;

  Multiplexer #(.width(8), .enable("false")) multiplexer_1 (
    .in0(Parameter), .in1(Bus_in), .out(multiplexer_1_out), .sel(decoder_1_out17));
  Pull_Resistor pull_resistor_1 (.node(multiplexer_1_out));
  Pull_Resistor pull_resistor_2 (.node(Interrpt_flag));
  Comparator comparator_1 (.a(multiplexer_1_out), .b(Interrpt_flag), .eq(comparator_1_eq));  // open: gt, lt
  Decoder #(.select(5), .enable("false")) decoder_1 (
    .out1(decoder_1_out1), .out2(decoder_1_out2), .out3(decoder_1_out3), .out4(decoder_1_out4),
    .out5(decoder_1_out5), .out6(decoder_1_out6), .out7(decoder_1_out7), .out8(decoder_1_out8),
    .out9(decoder_1_out9), .out10(Program_counter_increment), .out11(decoder_1_out11),
    .out12(decoder_1_out12), .out13(decoder_1_out13), .out14(decoder_1_out14), .out15(decoder_1_out15),
    .out16(decoder_1_out16), .out17(decoder_1_out17), .sel(Microcode[4:0]));  // open: out0, out18, out19, out20, out21, out22, out23, out24, out25, out26, out27, out28, out29, out30, out31
  and and_1 (and_1_out, comparator_1_eq, INT_out);
  assign controlled_buffer_1_out = not_1_out ? Interrupt : 1'bz;  // Controlled_Buffer controlled_buffer_1
  not not_1 (not_1_out, INT_out);
  or INT (INT_out, decoder_1_out16, decoder_1_out17);
  Multiplexer #(.width(8), .enable("false")) multiplexer_2 (
    .in0(Parameter), .in1({undriven, Cin_Bin}), .out(multiplexer_2_out), .sel(decoder_1_out8));
  or or_1 (or_1_out, decoder_1_out8, decoder_1_out3);
  Pull_Resistor pull_resistor_3 (.node(pull_resistor_3_node));
  or or_2 (or_2_out, pull_resistor_3_node, and_1_out, controlled_buffer_1_out);
  assign pull_resistor_3_node = s_r_ff_1_qn ? decoder_1_out9 : 1'bz;  // Controlled_Buffer controlled_buffer_2
  Comparator comparator_2 (.a(Bus_in), .b({8{1'b0}}), .eq(comparator_2_eq));  // open: gt, lt
  Pull_Resistor pull_resistor_4 (.node(pull_resistor_4_node));
  Multiplexer #(.width(8), .enable("false")) multiplexer_3 (
    .in0(Bus_in), .in1(multiplexer_2_out), .out(pull_resistor_4_node), .sel(or_1_out));
  Register register_1 (.D(pull_resistor_4_node), .en(not_3_out), .Q(register_1_q), .clk(Clock_out), .clr(Clear));
  not not_2 (not_2_out, Register_read);
  not not_3 (not_3_out, decoder_1_out2);
  S_R_Flip_Flop s_r_ff_1 (
    .S(pull_resistor_3_node), .clk(or_2_out), .R(controlled_buffer_1_out), .Q(Waiting), .Qn(s_r_ff_1_qn),
    .reset(Clear));  // open: preset, en
  Pull_Resistor pull_resistor_5 (.node(controlled_buffer_1_out));
  Adder adder_1 (.a(Address), .b(8'h1), .out(adder_1_out));  // open: cin, cout
  Register register_2 (.D(adder_1_out), .en(not_4_out), .Q(register_2_q), .clk(decoder_1_out12), .clr(Clear));
  not not_4 (not_4_out, decoder_1_out11);
  assign Bus_out = not_2_out ? register_1_q : 8'bz;  // Controlled_Buffer controlled_buffer_3
  and and_2 (Clock_out, Clock, ~controlled_buffer_1_out, s_r_ff_1_qn);  // AND_Gate
  Multiplexer #(.width(8), .enable("false")) multiplexer_4 (
    .in0(Parameter), .in1(Bus_in), .out(multiplexer_4_out), .sel(decoder_1_out7));
  Multiplexer #(.width(8), .enable("false")) multiplexer_5 (
    .in0(multiplexer_4_out), .in1(register_2_q), .out(multiplexer_5_out), .sel(decoder_1_out11));
  assign controlled_buffer_4_out = comparator_2_eq ? decoder_1_out4 : 1'bz;  // Controlled_Buffer controlled_buffer_4
  not not_5 (not_5_out, comparator_2_eq);
  assign Microcode_jump_address = Microcode_jump ? multiplexer_5_out : 8'bz;  // Controlled_Buffer controlled_buffer_5
  or JMP (Microcode_jump, 1'b0, controlled_buffer_4_out, controlled_buffer_6_out, decoder_1_out12, decoder_1_out6, decoder_1_out7, decoder_1_out11);
  or RD (Register_read, decoder_1_out1, decoder_1_out14);
  assign controlled_buffer_6_out = not_5_out ? decoder_1_out5 : 1'bz;  // Controlled_Buffer controlled_buffer_6
  or WR (Register_write, decoder_1_out2, decoder_1_out15);
  Multiplexer #(.width(8), .enable("false")) multiplexer_6 (
    .in0(Parameter), .in1(Bus_in), .out(multiplexer_6_out), .sel(decoder_1_out13));
  Register #(.trigger("high")) register_3 (
    .D(multiplexer_6_out), .Q(Register_select), .clk(RS_out), .clr(Clear));  // open: en
  or RS (RS_out, decoder_1_out1, decoder_1_out13, decoder_1_out2);
  Pull_Resistor pull_resistor_6 (.node(Register_select));
  Pull_Resistor pull_resistor_7 (.node(Microcode_jump_address));
  Pull_Resistor pull_resistor_8 (.node(Clock_out));
  Pull_Resistor pull_resistor_9 (.node(Bus_out));
  Pull_Resistor pull_resistor_10 (.node(controlled_buffer_4_out));
  Pull_Resistor pull_resistor_11 (.node(controlled_buffer_6_out));
  Pull_Resistor pull_resistor_12 (.node(decoder_1_out6));
  Pull_Resistor pull_resistor_13 (.node(decoder_1_out7));
  Pull_Resistor pull_resistor_14 (.node(decoder_1_out11));

  // Notes on the sheet:
  //   Microcode: pull=down
  //   Interrupt: pull=down
  //   Cin_Bin: pull=down
  //   Clock: pull=down
  //   Parameter: pull=down
  //   Bus_in: pull=down
  //   Clear: pull=down
endmodule

module RRD (
  input  [7:0] Register_value,
  input  [7:0] Register_address,
  input  [7:0] Select,
  input  Global_read,
  output [7:0] Bus_out,
  output Is_reading
);

  wire comparator_1_eq;

  Comparator comparator_1 (.a(Register_address), .b(Select), .eq(comparator_1_eq));  // open: gt, lt
  and and_1 (Is_reading, comparator_1_eq, Global_read);
  assign Bus_out = Is_reading ? Register_value : 8'bz;  // Controlled_Buffer controlled_buffer_1
endmodule

module EQU (
  input  [7:0] A,
  input  [7:0] B,
  input  E,
  output E_2
);

  wire comparator_1_eq;

  Comparator comparator_1 (.a(A), .b(B), .eq(comparator_1_eq));  // open: gt, lt
  and and_1 (E_2, comparator_1_eq, E);
endmodule

module REG (
  input  [7:0] Register_select,
  input  [7:0] Start,
  input  [7:0] Bus,
  input  Write,
  input  Clear,
  input  Read,
  input  Clear2,
  output [7:0] Out,
  output Reading
);

  wire equ_1_e_2, equ_2_e_2, equ_3_e_2, equ_4_e_2, or_1_out, pull_resistor_1_node, rrd_1_is_reading,
       rrd_2_is_reading, rrd_3_is_reading, rrd_4_is_reading;
  wire [7:0] register_1_q, register_2_q, register_3_q, register_4_q, rrd_1_bus_out;

  or or_1 (or_1_out, Clear2, Clear);
  EQU equ_1 (.A(Register_select), .B({Start[7:2], 2'b00}), .E(Write), .E_2(equ_1_e_2));
  EQU equ_2 (.A(Register_select), .B({Start[7:2], 2'b01}), .E(Write), .E_2(equ_2_e_2));
  EQU equ_3 (.A(Register_select), .B({Start[7:2], 2'b10}), .E(Write), .E_2(equ_3_e_2));
  EQU equ_4 (.A(Register_select), .B({Start[7:2], 2'b11}), .E(Write), .E_2(equ_4_e_2));
  Register register_1 (.D(Bus), .Q(register_1_q), .clk(equ_1_e_2), .clr(or_1_out));  // open: en
  Register register_2 (.D(Bus), .Q(register_2_q), .clk(equ_2_e_2), .clr(or_1_out));  // open: en
  Register register_3 (.D(Bus), .Q(register_3_q), .clk(equ_3_e_2), .clr(or_1_out));  // open: en
  Register register_4 (.D(Bus), .Q(register_4_q), .clk(equ_4_e_2), .clr(or_1_out));  // open: en
  RRD rrd_1 (
    .Register_value(register_1_q), .Register_address({Start[7:2], 2'b00}), .Select(Register_select),
    .Global_read(Read), .Bus_out(rrd_1_bus_out), .Is_reading(rrd_1_is_reading));
  RRD rrd_2 (
    .Register_value(register_2_q), .Register_address({Start[7:2], 2'b01}), .Select(Register_select),
    .Global_read(Read), .Bus_out(rrd_1_bus_out), .Is_reading(rrd_2_is_reading));
  RRD rrd_3 (
    .Register_value(register_3_q), .Register_address({Start[7:2], 2'b10}), .Select(Register_select),
    .Global_read(Read), .Bus_out(rrd_1_bus_out), .Is_reading(rrd_3_is_reading));
  RRD rrd_4 (
    .Register_value(register_4_q), .Register_address({Start[7:2], 2'b11}), .Select(Register_select),
    .Global_read(Read), .Bus_out(rrd_1_bus_out), .Is_reading(rrd_4_is_reading));
  or or_2 (Reading, rrd_1_is_reading, rrd_2_is_reading, rrd_3_is_reading, rrd_4_is_reading);
  Pull_Resistor pull_resistor_1 (.node(pull_resistor_1_node));
  assign Out = Reading ? rrd_1_bus_out : 8'bz;  // Controlled_Buffer controlled_buffer_1

  // Notes on the sheet:
  //   Clear2: pull=down
  //   Microcode registers
  //   Used by the microcode to store shit, like the GPR but for the microcode
endmodule

// MCTR
module Microcode_counter (
  input  [15:0] Data,
  input  [7:0] Address,
  input  Jump,
  input  Clock,
  input  Reset,
  output [7:0] Instruction,
  output [7:0] Parameter,
  output [7:0] Address_2
);

  wire not_1_out;

  Counter counter_1 (
    .load(Jump), .D(Address), .count(not_1_out), .Q(Address_2), .clk(Clock), .clr(Reset));  // open: carry
  not not_1 (not_1_out, Jump);

  assign Instruction = Data[15:8];
  assign Parameter = Data[7:0];
endmodule

module Register_buffer (
  input  [7:0] Data_in,
  input  [7:0] Register_select,
  input  [7:0] Address,
  input  Write,
  input  Clear,
  output [7:0] Data_out
);

  wire equ_1_e_2;

  Register register_1 (.D(Data_in), .Q(Data_out), .clk(equ_1_e_2), .clr(Clear));  // open: en
  EQU equ_1 (.A(Address), .B(Register_select), .E(Write), .E_2(equ_1_e_2));
endmodule

module Entry (
  input  _0,
  input  _1,
  input  _2,
  input  _3,
  input  _4,
  input  _5,
  input  _6,
  input  _7,
  input  Zero_all,
  input  Enable,
  input  One_all,
  output [7:0] Value,
  output _0_2,
  output _1_2,
  output _2_2,
  output _3_2,
  output _4_2,
  output _5_2,
  output _6_2,
  output _7_2
);

  T_Flip_Flop t_ff_1 (.clk(_0), .T(_0), .Q(_0_2), .preset(One_all), .reset(Zero_all), .en(Enable));  // open: Qn
  T_Flip_Flop t_ff_2 (.clk(_1), .T(_1), .Q(_1_2), .preset(One_all), .reset(Zero_all), .en(Enable));  // open: Qn
  T_Flip_Flop t_ff_3 (.clk(_2), .T(_2), .Q(_2_2), .preset(One_all), .reset(Zero_all), .en(Enable));  // open: Qn
  T_Flip_Flop t_ff_4 (.clk(_3), .T(_3), .Q(_3_2), .preset(One_all), .reset(Zero_all), .en(Enable));  // open: Qn
  T_Flip_Flop t_ff_5 (.clk(_4), .T(_4), .Q(_4_2), .preset(One_all), .reset(Zero_all), .en(Enable));  // open: Qn
  T_Flip_Flop t_ff_6 (.clk(_5), .T(_5), .Q(_5_2), .preset(One_all), .reset(Zero_all), .en(Enable));  // open: Qn
  T_Flip_Flop t_ff_7 (.clk(_6), .T(_6), .Q(_6_2), .preset(One_all), .reset(Zero_all), .en(Enable));  // open: Qn
  T_Flip_Flop t_ff_8 (.clk(_7), .T(_7), .Q(_7_2), .preset(One_all), .reset(Zero_all), .en(Enable));  // open: Qn
  Pull_Resistor pull_resistor_1 (.node(Zero_all));
  Pull_Resistor #(.pull(1)) pull_resistor_2 (.node(Enable));
  Pull_Resistor pull_resistor_3 (.node(One_all));

  assign Value = {_0_2, _1_2, _2_2, _3_2, _4_2, _5_2, _6_2, _7_2};

  // Notes on the sheet:
  //   Zero_all: pull=down
  //   One_all: pull=down
  //   Enable: pull=up
endmodule

module Compare_and_pass (
  input  [7:0] A,
  input  [7:0] B,
  input  _1__or____0,
  output [7:0] Out
);

  wire comparator_1_lt, multiplexer_1_out, not_1_out;

  Comparator #(.mode("unsigned")) comparator_1 (.a(B), .b(A), .lt(comparator_1_lt));  // open: gt, eq
  Multiplexer #(.enable("false")) multiplexer_1 (
    .in0(comparator_1_lt), .in1(not_1_out), .out(multiplexer_1_out), .sel(_1__or____0));
  not not_1 (not_1_out, comparator_1_lt);
  Multiplexer #(.width(8), .enable("false")) multiplexer_2 (.in0(A), .in1(B), .out(Out), .sel(multiplexer_1_out));
endmodule

// Logic
module ALU_logical_block (
  input  [7:0] A,
  input  [7:0] B,
  output [7:0] A_2,
  output [7:0] B_2,
  output [7:0] NOT_A,
  output [7:0] NOT_B,
  output [7:0] AND,
  output [7:0] OR,
  output [7:0] XOR,
  output [7:0] IMPLY_A,
  output [7:0] IMPLY_B,
  output [7:0] Pass_lesser,
  output [7:0] Pass_greater
);

  wire comparator_1_lt, comparator_2_lt, not_3_out;

  assign NOT_A = ~A;  // NOT_Gate not_1, 8 bits wide
  assign NOT_B = ~B;  // NOT_Gate not_2, 8 bits wide
  assign AND = A & B;  // AND_Gate and_1, 8 bits wide
  assign OR = A | B;  // OR_Gate or_1, 8 bits wide
  assign XOR = A ^ B;  // XOR_Gate xor_1, 8 bits wide
  assign IMPLY_A = ~A | B;  // OR_Gate or_2, 8 bits wide
  assign IMPLY_B = A | ~B;  // OR_Gate or_3, 8 bits wide
  not not_3 (not_3_out, comparator_1_lt);
  Comparator #(.mode("unsigned")) comparator_1 (.a(A), .b(B), .lt(comparator_1_lt));  // open: gt, eq
  Comparator #(.mode("unsigned")) comparator_2 (.a(A), .b(B), .lt(comparator_2_lt));  // open: gt, eq
  Multiplexer #(.width(8), .enable("false")) multiplexer_1 (.in0(A), .in1(B), .out(Pass_lesser), .sel(not_3_out));
  Multiplexer #(.width(8), .enable("false")) multiplexer_2 (
    .in0(A), .in1(B), .out(Pass_greater), .sel(comparator_2_lt));

  assign A_2 = A;
  assign B_2 = B;
endmodule

// ALU
module ALU_V2 (
  input  [7:0] Data,
  input  [7:0] Register_select,
  input  Global_write,
  input  Global_read,
  input  Clear,
  output [7:0] Output,
  output Reading,
  output Cout_Bout
);

  wire comparator_1_eq, comparator_2_eq, comparator_3_eq, equ_1_e_2, equ_2_e_2, equ_3_e_2,
       pull_resistor_1_node, pull_resistor_2_node, pull_resistor_3_node;
  wire [2:0] alu_arithmetic_block_1_cout_bout1_bout2;
  wire [7:0] alu_arithmetic_block_1_a___b, alu_arithmetic_block_1_a___b_2, alu_arithmetic_block_1_b___a,
       alu_arithmetic_block_1_left_shift_a_by_b, alu_arithmetic_block_1_minus_a,
       alu_arithmetic_block_1_minus_b, alu_arithmetic_block_1_right_shift_a_by_b,
       alu_arithmetic_block_1_rotate_a_left_by_b, alu_arithmetic_block_1_rotate_a_right_by_b,
       alu_arithmetic_block_1_select_bit_b_from_a, alu_logical_block_1_a_2, alu_logical_block_1_and,
       alu_logical_block_1_b_2, alu_logical_block_1_imply_a, alu_logical_block_1_imply_b,
       alu_logical_block_1_not_a, alu_logical_block_1_not_b, alu_logical_block_1_or,
       alu_logical_block_1_pass_greater, alu_logical_block_1_pass_lesser, alu_logical_block_1_xor,
       multiplexer_1_out, multiplexer_2_out, multiplexer_3_out, not_1_out, register_1_q, register_2_q,
       register_3_q, shifter_1_out, shifter_2_out, shifter_3_out;

  EQU equ_1 (.A(Register_select), .B(8'h10), .E(Global_write), .E_2(equ_1_e_2));
  EQU equ_2 (.A(Register_select), .B(8'h11), .E(Global_write), .E_2(equ_2_e_2));
  EQU equ_3 (.A(Register_select), .B(8'h12), .E(Global_write), .E_2(equ_3_e_2));
  EQU equ_4 (.A(Register_select), .B(8'h13), .E(Global_read), .E_2(Reading));
  Register register_1 (.D(Data), .Q(register_1_q), .clk(equ_1_e_2), .clr(Clear));  // open: en
  Register register_2 (.D(Data), .Q(register_2_q), .clk(equ_2_e_2), .clr(Clear));  // open: en
  Register register_3 (.D(Data), .Q(register_3_q), .clk(equ_3_e_2), .clr(Clear));  // open: en
  ALU_logical_block alu_logical_block_1 (
    .A(register_1_q), .B(register_2_q), .A_2(alu_logical_block_1_a_2), .B_2(alu_logical_block_1_b_2),
    .NOT_A(alu_logical_block_1_not_a), .NOT_B(alu_logical_block_1_not_b), .AND(alu_logical_block_1_and),
    .OR(alu_logical_block_1_or), .XOR(alu_logical_block_1_xor), .IMPLY_A(alu_logical_block_1_imply_a),
    .IMPLY_B(alu_logical_block_1_imply_b), .Pass_lesser(alu_logical_block_1_pass_lesser),
    .Pass_greater(alu_logical_block_1_pass_greater));
  ALU_Arithmetic_block alu_arithmetic_block_1 (
    .A(register_1_q), .B(register_2_q), .Cout_Bout1_Bout2(alu_arithmetic_block_1_cout_bout1_bout2),
    .A___B(alu_arithmetic_block_1_a___b), .A___B_2(alu_arithmetic_block_1_a___b_2),
    .B___A(alu_arithmetic_block_1_b___a), .minus_A(alu_arithmetic_block_1_minus_a),
    .minus_B(alu_arithmetic_block_1_minus_b), .Left_shift_A_by_B(alu_arithmetic_block_1_left_shift_a_by_b),
    .Right_shift_A_by_B(alu_arithmetic_block_1_right_shift_a_by_b),
    .Rotate_A_left_by_B(alu_arithmetic_block_1_rotate_a_left_by_b),
    .Rotate_A_right_by_B(alu_arithmetic_block_1_rotate_a_right_by_b),
    .Select_bit_B_from_A(alu_arithmetic_block_1_select_bit_b_from_a));
  Multiplexer #(.select(5), .width(8), .enable("false")) multiplexer_1 (
    .in0(alu_logical_block_1_a_2), .in1(alu_logical_block_1_b_2), .in2(alu_logical_block_1_not_a),
    .in3(alu_logical_block_1_not_b), .in4(alu_logical_block_1_and), .in5(alu_logical_block_1_or),
    .in6(alu_logical_block_1_xor), .in7(alu_logical_block_1_imply_a), .in8(alu_logical_block_1_imply_b),
    .in9(alu_logical_block_1_pass_lesser), .in10(alu_logical_block_1_pass_greater), .in11({8{1'b1}}),
    .in12({8{1'b0}}), .in13(alu_arithmetic_block_1_a___b), .in14(alu_arithmetic_block_1_a___b_2),
    .in15(alu_arithmetic_block_1_b___a), .in16(alu_arithmetic_block_1_minus_a),
    .in17(alu_arithmetic_block_1_minus_b), .in18(alu_arithmetic_block_1_left_shift_a_by_b),
    .in19(alu_arithmetic_block_1_right_shift_a_by_b), .in20(alu_arithmetic_block_1_rotate_a_left_by_b),
    .in21(alu_arithmetic_block_1_rotate_a_right_by_b), .in22(alu_arithmetic_block_1_select_bit_b_from_a),
    .out(multiplexer_1_out), .sel(register_3_q[4:0]));  // open: in23, in24, in25, in26, in27, in28, in29, in30, in31
  Shifter #(.shift("ar")) shifter_1 (.in(multiplexer_1_out), .\dist (3'b001), .out(shifter_1_out));
  Shifter shifter_2 (.in(multiplexer_1_out), .\dist (3'b001), .out(shifter_2_out));
  Shifter #(.shift("lr")) shifter_3 (.in(multiplexer_1_out), .\dist (3'b001), .out(shifter_3_out));
  Comparator #(.width(5), .mode("unsigned")) comparator_1 (
    .a(register_3_q[4:0]), .b(5'b01101), .eq(comparator_1_eq));  // open: gt, lt
  Comparator #(.width(5), .mode("unsigned")) comparator_2 (
    .a(register_3_q[4:0]), .b(5'b01110), .eq(comparator_2_eq));  // open: gt, lt
  Comparator #(.width(5), .mode("unsigned")) comparator_3 (
    .a(register_3_q[4:0]), .b(5'b01111), .eq(comparator_3_eq));  // open: gt, lt
  Multiplexer #(.select(2), .width(8), .enable("false")) multiplexer_2 (
    .in0(multiplexer_1_out), .in1(shifter_1_out), .in2(shifter_2_out), .in3(shifter_3_out),
    .out(multiplexer_2_out), .sel(register_3_q[6:5]));
  assign not_1_out = ~multiplexer_2_out;  // NOT_Gate not_1, 8 bits wide
  or or_1 (Cout_Bout, pull_resistor_1_node, pull_resistor_2_node, pull_resistor_3_node);
  Pull_Resistor pull_resistor_1 (.node(pull_resistor_1_node));
  assign pull_resistor_1_node = comparator_1_eq ? alu_arithmetic_block_1_cout_bout1_bout2[0] : 1'bz;  // Controlled_Buffer controlled_buffer_1
  Pull_Resistor pull_resistor_2 (.node(pull_resistor_2_node));
  Pull_Resistor pull_resistor_3 (.node(pull_resistor_3_node));
  assign pull_resistor_2_node = comparator_2_eq ? alu_arithmetic_block_1_cout_bout1_bout2[1] : 1'bz;  // Controlled_Buffer controlled_buffer_2
  assign pull_resistor_3_node = comparator_3_eq ? alu_arithmetic_block_1_cout_bout1_bout2[2] : 1'bz;  // Controlled_Buffer controlled_buffer_3
  Multiplexer #(.width(8), .enable("false")) multiplexer_3 (
    .in0(multiplexer_2_out), .in1(not_1_out), .out(multiplexer_3_out), .sel(register_3_q[7]));
  assign Output = Reading ? multiplexer_3_out : 8'bz;  // Controlled_Buffer controlled_buffer_4

  // Other names for the same wires on the sheet: R = Reading

  // Notes on the sheet:
  //   Cout_Bout: pull=down
  //   A
  //   B
  //   OPC
  //   OUT
endmodule

// Arith
module ALU_Arithmetic_block (
  input  [7:0] A,
  input  [7:0] B,
  output [2:0] Cout_Bout1_Bout2,
  output [7:0] A___B,
  output [7:0] A___B_2,
  output [7:0] B___A,
  output [7:0] minus_A,
  output [7:0] minus_B,
  output [7:0] Left_shift_A_by_B,
  output [7:0] Right_shift_A_by_B,
  output [7:0] Rotate_A_left_by_B,
  output [7:0] Rotate_A_right_by_B,
  output [7:0] Select_bit_B_from_A
);

  Adder adder_1 (.a(A), .b(B), .out(A___B), .cout(Cout_Bout1_Bout2[0]));  // open: cin
  Subtractor subtractor_1 (.a(A), .b(B), .out(A___B_2), .bout(Cout_Bout1_Bout2[1]));  // open: bin
  Subtractor subtractor_2 (.a(B), .b(A), .out(B___A), .bout(Cout_Bout1_Bout2[2]));  // open: bin
  Negator negator_1 (.in(A), .out(minus_A));
  Negator negator_2 (.in(B), .out(minus_B));
  Shifter shifter_1 (.in(A), .\dist (B[2:0]), .out(Left_shift_A_by_B));
  Shifter #(.shift("lr")) shifter_2 (.in(A), .\dist (B[2:0]), .out(Right_shift_A_by_B));
  Shifter #(.shift("rl")) shifter_3 (.in(A), .\dist (B[2:0]), .out(Rotate_A_left_by_B));
  Shifter #(.shift("rr")) shifter_4 (.in(A), .\dist (B[2:0]), .out(Rotate_A_right_by_B));
  BitSelector bitselector_1 (.in(A), .out(Select_bit_B_from_A[0]), .sel(B[2:0]));
endmodule

// REG
module REG_BANK (
  input  [7:0] Bus_in,
  input  [7:0] Register_select,
  input  Write,
  input  Read,
  input  Clear,
  input  PCI,
  output [7:0] Out,
  output Is_reading
);

  wire reg_1_reading, reg_2_reading, reg_3_reading, reg_4_reading, reg_5_reading, reg_6_reading;
  wire [7:0] reg_1_out;

  REG reg_1 (
    .Register_select(Register_select), .Bus(Bus_in), .Write(Write), .Clear(Clear), .Read(Read),
    .Out(reg_1_out), .Reading(reg_1_reading), .Clear2(PCI), .Start(8'h20));
  REG reg_2 (
    .Register_select(Register_select), .Bus(Bus_in), .Write(Write), .Clear(Clear), .Read(Read),
    .Out(reg_1_out), .Reading(reg_2_reading), .Clear2(1'b0), .Start(8'h24));
  REG reg_3 (
    .Register_select(Register_select), .Bus(Bus_in), .Write(Write), .Clear(Clear), .Read(Read),
    .Out(reg_1_out), .Reading(reg_3_reading), .Clear2(1'b0), .Start(8'h30));
  REG reg_4 (
    .Register_select(Register_select), .Bus(Bus_in), .Write(Write), .Clear(Clear), .Read(Read),
    .Out(reg_1_out), .Reading(reg_4_reading), .Clear2(1'b0), .Start(8'h34));
  REG reg_5 (
    .Register_select(Register_select), .Bus(Bus_in), .Write(Write), .Clear(Clear), .Read(Read),
    .Out(reg_1_out), .Reading(reg_5_reading), .Clear2(1'b0), .Start(8'h38));
  REG reg_6 (
    .Register_select(Register_select), .Bus(Bus_in), .Write(Write), .Clear(Clear), .Read(Read),
    .Out(reg_1_out), .Reading(reg_6_reading), .Clear2(1'b0), .Start(8'h3c));
  assign Out = Is_reading ? reg_1_out : 8'bz;  // Controlled_Buffer controlled_buffer_1
  or or_1 (Is_reading, reg_1_reading, reg_2_reading, reg_3_reading, reg_4_reading, reg_5_reading, reg_6_reading);
endmodule

module Microcode_ROM (
  input  [15:0] Address,
  input  [7:0] Instruction,
  input  PCI_Fucking_now,
  input  [7:0] Microcode_address,
  output [15:0] Microcode_out,
  output ITS_THE_GOD_DAMN_END_OF_THE_FUCKING_WORLD__or_program
);

  wire [15:0] adder_1_out, rom_1_data;
  wire [15:8] undriven;

  Adder #(.width(16)) adder_1 (
    .a(rom_1_data), .b({undriven, Microcode_address}), .out(adder_1_out),
    .cout(ITS_THE_GOD_DAMN_END_OF_THE_FUCKING_WORLD__or_program));  // open: cin
  ROM #(.dataWidth(16)) rom_1 (.addr(Instruction), .data(rom_1_data));  // open: sel
  ROM #(.addrWidth(16), .dataWidth(16)) rom_2 (.addr(adder_1_out), .data(Microcode_out));  // open: sel

  // Notes on the sheet:
  //   Microcode offset table
  //   Microcode ROM
endmodule
